// Logisim project ALU.circ as structural Verilog
module ALU4Bit (
  input  [3:0] A,
  input  [3:0] B,
  input  [3:0] C,
  output Zero,
  output Overflow,
  output [3:0] R
);

  wire alu1bit_1_carryout, alu1bit_2_carryout, alu1bit_3_carryout, alu1bit_4_carryout, alu1bit_4_set,
       carryinsetter_1_initcarry, nor_1_out, nor_2_out, xor_2_out;

  // Probe on A
  // Probe on B
  CarryInSetter carryinsetter_1 (.C2(C[2]), .C1(C[1]), .C3(C[3]), .C0(C[0]), .InitCarry(carryinsetter_1_initcarry));
  ALU1Bit alu1bit_1 (
    .Result(R[0]), .B(B[0]), .A(A[0]), .Operation(C[1:0]), .CarryIn(carryinsetter_1_initcarry),
    .BInvert(C[2]), .AInvert(C[3]), .CarryOut(alu1bit_1_carryout), .Less(xor_2_out));  // open: Set
  ALU1Bit alu1bit_2 (
    .Result(R[1]), .B(B[1]), .A(A[1]), .Operation(C[1:0]), .CarryIn(alu1bit_1_carryout), .BInvert(C[2]),
    .AInvert(C[3]), .CarryOut(alu1bit_2_carryout));  // open: Set, Less
  ALU1Bit alu1bit_3 (
    .Result(R[2]), .B(B[2]), .A(A[2]), .Operation(C[1:0]), .CarryIn(alu1bit_2_carryout), .BInvert(C[2]),
    .AInvert(C[3]), .CarryOut(alu1bit_3_carryout));  // open: Set, Less
  ALU1Bit alu1bit_4 (
    .Result(R[3]), .B(B[3]), .A(A[3]), .Operation(C[1:0]), .CarryIn(alu1bit_3_carryout), .BInvert(C[2]),
    .AInvert(C[3]), .CarryOut(alu1bit_4_carryout), .Set(alu1bit_4_set));  // open: Less
  // Probe on R
  and and_1 (Zero, nor_1_out, nor_2_out);
  nor nor_1 (nor_1_out, R[0], R[1]);
  nor nor_2 (nor_2_out, R[2], R[3]);
  xor xor_1 (Overflow, alu1bit_3_carryout, alu1bit_4_carryout);
  xor xor_2 (xor_2_out, Overflow, alu1bit_4_set);

  // Notes on the sheet:
  //   Jordan Miller 260513815
endmodule

module ALU1Bit (
  input  AInvert,
  input  BInvert,
  input  CarryIn,
  input  [1:0] Operation,
  input  A,
  input  B,
  input  Less,
  output Result,
  output Set,
  output CarryOut
);

  wire and_1_out, or_1_out, xor_1_out, xor_2_out;

  xor xor_1 (xor_1_out, AInvert, A);
  xor xor_2 (xor_2_out, BInvert, B);
  and and_1 (and_1_out, xor_1_out, xor_2_out);
  or or_1 (or_1_out, xor_1_out, xor_2_out);
  Add add_1 (.Cin(CarryIn), .Sum(Set), .A(xor_1_out), .Cout(CarryOut), .B(xor_2_out));
  Mux mux_1 (.D0(and_1_out), .D1(or_1_out), .D2(Set), .D3(Less), .S0(Operation[0]), .S1(Operation[1]), .MuxOut(Result));

  // Notes on the sheet:
  //   Jordan Miller 260513815
endmodule

module Add (
  input  Cin,
  input  A,
  input  B,
  output Sum,
  output Cout
);

  wire halfadder_1_cout, halfadder_1_sum, halfadder_2_cout;

  HalfAdder halfadder_1 (.A(A), .B(B), .Sum(halfadder_1_sum), .Cout(halfadder_1_cout));
  HalfAdder halfadder_2 (.A(Cin), .B(halfadder_1_sum), .Sum(Sum), .Cout(halfadder_2_cout));
  or or_1 (Cout, halfadder_2_cout, halfadder_1_cout);

  // Notes on the sheet:
  //   Jordan Miller 260513815
endmodule

module Decode (
  input  S0,
  input  S1,
  output D0,
  output D1,
  output D2,
  output D3
);

  wire not_1_out, not_2_out;

  not not_1 (not_1_out, S1);
  not not_2 (not_2_out, S0);
  and and_1 (D1, S0, not_1_out);
  and and_2 (D2, not_2_out, S1);
  and and_3 (D3, S0, S1);
  nor nor_1 (D0, S0, S1);

  // Notes on the sheet:
  //   Jordan Miller 260513815
endmodule

module Mux (
  input  S1,
  input  S0,
  input  D0,
  input  D1,
  input  D2,
  input  D3,
  output MuxOut
);

  wire and_1_out, and_2_out, and_3_out, and_4_out, decode_1_d0, decode_1_d1, decode_1_d2, decode_1_d3,
       or_1_out, or_2_out;

  Decode decode_1 (.S0(S0), .S1(S1), .D0(decode_1_d0), .D1(decode_1_d1), .D2(decode_1_d2), .D3(decode_1_d3));
  and and_1 (and_1_out, decode_1_d0, D0);
  and and_2 (and_2_out, decode_1_d1, D1);
  and and_3 (and_3_out, decode_1_d2, D2);
  and and_4 (and_4_out, decode_1_d3, D3);
  or or_1 (or_1_out, and_1_out, and_2_out);
  or or_2 (or_2_out, or_1_out, and_3_out);
  or or_3 (MuxOut, or_2_out, and_4_out);

  // Notes on the sheet:
  //   Jordan Miller 260513815
endmodule

module HalfAdder (
  input  A,
  input  B,
  output Sum,
  output Cout
);

  wire not_1_out, or_1_out;

  or or_1 (or_1_out, A, B);
  not not_1 (not_1_out, Cout);
  and and_1 (Cout, A, B);
  and and_2 (Sum, or_1_out, not_1_out);
endmodule

module CarryInSetter (
  input  C0,
  input  C1,
  input  C2,
  input  C3,
  output InitCarry
);

  wire and_1_out, and_2_out, and_3_out, and_4_out, and_5_out, nor_1_out, not_1_out;

  nor nor_1 (nor_1_out, C0, C3);
  and and_1 (and_1_out, C1, C2);
  not not_1 (not_1_out, C3);
  and and_2 (and_2_out, C0, C1);
  and and_3 (and_3_out, C2, not_1_out);
  and and_4 (and_4_out, nor_1_out, and_1_out);
  and and_5 (and_5_out, and_2_out, and_3_out);
  or or_1 (InitCarry, and_4_out, and_5_out);
endmodule
